# Fritzing sketch 3 (saved by Fritzing 0.9.10b)
breadboards: 1

parts:
  Mod1 = Raspberry Pi Pico W
  LED1 = LED - 5mm [color="Red (633nm)" current=0.030 package="5 mm [THT]"]  # not connected
  LED2 = smd LED [color="Red (633nm)" package="1206 [SMD]"]
  S1 = Pushbutton [package="[THT]"]

nets:
  N1: Mod1.pin_3, Mod1.pin_8, Mod1.pin_13, Mod1.pin_18, Mod1.pin_23, Mod1.pin_28, Mod1.pin_33, Mod1.pin_38, Mod1.pin_42, LED2.cathode
  N2: Mod1.pin_20, LED2.anode
  N3: Mod1.pin_21, S1.Pin_3, S1.Pin_4
  N4: Mod1.pin_36, S1.Pin_1, S1.Pin_2

notes:
  GND
  + 3.3V
  (GPIO 15<module fritzingVersion="0.9.10b.2022-05-14.0.9.6-336-g29c2cede">
  <boundingRects>
  <boundingRect name="PCB View" rect="0 0 0 0"/>
  <boundingRect name="Schematic View" rect="0 0 0 0"/>
  <boundingRect name="Breadboard View" rect="-1.74105 -61.7657 43.1212 37.5202"/>
  </boundingRects>
  <instances>
  <instance moduleIdRef="NoteModuleID" modelIndex="6549" path=":/resources/parts/core/note.fzp">
  <title>Note10</title>
  <text>&lt;!DOCTYPE HTML PUBLIC "-//W3C//DTD HTML 4.0//EN" "http://www.w3.org/TR/REC-html40/strict.dtd">
  &lt;html>&lt;head>&lt;meta name="qrichtext" content="1" />&lt;style type="text/css">
  p, li { white-space: pre-wrap; }
  &lt;/style>&lt;/head>&lt;body style=" font-family:'Droid Sans'; font-size:9pt; font-weight:400; font-style:normal;">
  &lt;p style=" margin-top:0px; margin-bottom:0px; margin-left:0px; margin-right:0px; -qt-block-indent:0; text-indent:0px;">GND &lt;/p>&lt;/body>&lt;/html></text>
  <views>
  <breadboardView layer="breadboardNote">
  <geometry y="-61.7657" z="6" x="-1.74105" width="43.1212" height="37.5202"/>
  </breadboardView>
  </views>
  </instance>
  </instances>
  </module>
  )
  3.3 V
  INPUT
  (GPIO 16)

custom parts:
  Raspberry Pi Pico W: Raspberry Pi Pico W. Based around the RP2040 microcontroller the Pico W is a low cost microcontroller device bringing Raspberry Pi quality, cost, and easy of use to the microcontroller space. The areas marked KEEPOUT in pcb silkscreen should not have traces running through them to avoid shorts on a soldered in module!
