# Fritzing sketch 4c (saved by Fritzing 0.9.10b)
breadboards: 1

parts:
  Mod1 = Raspberry Pi Pico W
  LCM1602_IIC1 = LCM1602 IIC [part_number="LCM1602 IIC" chip_label="LCM1602 IIC" package="DIP (Dual Inline) [THT]"]
  LCD1 = LCD screen

nets:
  N1: Mod1.pin_1, Mod1.pin_6, LCM1602_IIC1.SDA
  N2: Mod1.pin_2, Mod1.pin_12, LCM1602_IIC1.SCL
  N3: Mod1.pin_3, Mod1.pin_8, Mod1.pin_13, Mod1.pin_18, Mod1.pin_23, Mod1.pin_28, Mod1.pin_33, Mod1.pin_38, LCM1602_IIC1.GND
  VSS: Mod1.pin_40, LCM1602_IIC1.VSS, LCM1602_IIC1.VDD, LCM1602_IIC1.V0, LCM1602_IIC1.RS, LCM1602_IIC1.RW, LCM1602_IIC1.D0, LCM1602_IIC1.D1, LCM1602_IIC1.D2, LCM1602_IIC1.D3, LCM1602_IIC1.D4, LCM1602_IIC1.D6, LCM1602_IIC1.D7, LCM1602_IIC1.A, LCM1602_IIC1.K, LCM1602_IIC1.VCC, LCD1.VSS, LCD1.VDD, LCD1.V0, LCD1.RS, LCD1.R/W, LCD1.DB0, LCD1.DB1, LCD1.DB2, LCD1.DB3, LCD1.DB4, LCD1.DB6, LCD1.DB7, LCD1.LED+, LCD1.LED-
  N4: LCM1602_IIC1.E, LCD1.E
  N5: LCM1602_IIC1.D5, LCD1.DB5

notes:
  5V
  GND
  SDA
  SCL

custom parts:
  Raspberry Pi Pico W: Raspberry Pi Pico W. Based around the RP2040 microcontroller the Pico W is a low cost microcontroller device bringing Raspberry Pi quality, cost, and easy of use to the microcontroller space. The areas marked KEEPOUT in pcb silkscreen should not have traces running through them to avoid shorts on a soldered in module!
  LCM1602 IIC: I2C-Module to use a 1602 or 2004 LCD on with the wire.h libory Serial LCD Modul
